// Logisim project 7segment.circ as structural Verilog: 1 circuit, main circuit main
module main (
  input  [7:0] in_1,
  input  [7:0] in_2,
  input  [7:0] in_3,
  input  [7:0] in_4,
  input  [7:0] in_5,
  input  [7:0] in_6,
  input  [7:0] in_7,
  input  [7:0] in_8,
  output c,
  output a,
  output [3:0] harf_sayisi,
  output b,
  output d,
  output e,
  output g,
  output f
);

  wire comparator_1_gt, comparator_2_gt, comparator_3_gt, comparator_4_gt, comparator_5_gt, comparator_6_gt,
       comparator_7_gt, comparator_8_gt, comparator_9_eq, comparator_10_eq, comparator_11_eq,
       comparator_12_eq, comparator_13_eq, comparator_14_eq, comparator_15_eq, comparator_16_eq,
       comparator_17_eq;
  wire [3:0] adder_1_out, adder_2_out, adder_3_out, adder_4_out, adder_5_out, adder_6_out,
       bit_extender_1_out, bit_extender_2_out, bit_extender_3_out, bit_extender_4_out, bit_extender_5_out,
       bit_extender_6_out, bit_extender_7_out, bit_extender_8_out;

  Comparator #(.mode("unsigned")) comparator_1 (.a(in_1), .b({8{1'b0}}), .gt(comparator_1_gt));  // open: eq, lt
  Comparator #(.mode("unsigned")) comparator_2 (.a(in_2), .b({8{1'b0}}), .gt(comparator_2_gt));  // open: eq, lt
  Comparator #(.mode("unsigned")) comparator_3 (.a(in_3), .b({8{1'b0}}), .gt(comparator_3_gt));  // open: eq, lt
  Comparator #(.mode("unsigned")) comparator_4 (.a(in_4), .b({8{1'b0}}), .gt(comparator_4_gt));  // open: eq, lt
  Comparator #(.mode("unsigned")) comparator_5 (.a(in_5), .b({8{1'b0}}), .gt(comparator_5_gt));  // open: eq, lt
  Comparator #(.mode("unsigned")) comparator_6 (.a(in_6), .b({8{1'b0}}), .gt(comparator_6_gt));  // open: eq, lt
  Comparator #(.mode("unsigned")) comparator_7 (.a(in_7), .b({8{1'b0}}), .gt(comparator_7_gt));  // open: eq, lt
  Comparator #(.mode("unsigned")) comparator_8 (.a(in_8), .b({8{1'b0}}), .gt(comparator_8_gt));  // open: eq, lt
  assign bit_extender_1_out = {{3{1'b0}}, comparator_1_gt};  // Bit_Extender bit_extender_1
  assign bit_extender_2_out = {{3{1'b0}}, comparator_2_gt};  // Bit_Extender bit_extender_2
  assign bit_extender_3_out = {{3{1'b0}}, comparator_3_gt};  // Bit_Extender bit_extender_3
  assign bit_extender_4_out = {{3{1'b0}}, comparator_4_gt};  // Bit_Extender bit_extender_4
  assign bit_extender_5_out = {{3{1'b0}}, comparator_5_gt};  // Bit_Extender bit_extender_5
  assign bit_extender_6_out = {{3{1'b0}}, comparator_6_gt};  // Bit_Extender bit_extender_6
  assign bit_extender_7_out = {{3{1'b0}}, comparator_7_gt};  // Bit_Extender bit_extender_7
  assign bit_extender_8_out = {{3{1'b0}}, comparator_8_gt};  // Bit_Extender bit_extender_8
  Adder #(.width(4)) adder_1 (.a(bit_extender_1_out), .b(bit_extender_2_out), .out(adder_1_out));  // open: cin, cout
  Adder #(.width(4)) adder_2 (.a(bit_extender_3_out), .b(bit_extender_4_out), .out(adder_2_out));  // open: cin, cout
  Adder #(.width(4)) adder_3 (.a(bit_extender_5_out), .b(bit_extender_6_out), .out(adder_3_out));  // open: cin, cout
  Adder #(.width(4)) adder_4 (.a(bit_extender_7_out), .b(bit_extender_8_out), .out(adder_4_out));  // open: cin, cout
  Adder #(.width(4)) adder_5 (.a(adder_1_out), .b(adder_2_out), .out(adder_5_out));  // open: cin, cout
  Adder #(.width(4)) adder_6 (.a(adder_3_out), .b(adder_4_out), .out(adder_6_out));  // open: cin, cout
  Adder #(.width(4)) adder_7 (.a(adder_5_out), .b(adder_6_out), .out(harf_sayisi));  // open: cin, cout
  Comparator #(.width(4), .mode("unsigned")) comparator_9 (
    .a(harf_sayisi), .b(4'b0000), .eq(comparator_9_eq));  // open: gt, lt
  Comparator #(.width(4), .mode("unsigned")) comparator_10 (
    .a(harf_sayisi), .b(4'b0001), .eq(comparator_10_eq));  // open: gt, lt
  Comparator #(.width(4), .mode("unsigned")) comparator_11 (
    .a(harf_sayisi), .b(4'b0010), .eq(comparator_11_eq));  // open: gt, lt
  Comparator #(.width(4), .mode("unsigned")) comparator_12 (
    .a(harf_sayisi), .b(4'b0011), .eq(comparator_12_eq));  // open: gt, lt
  Comparator #(.width(4), .mode("unsigned")) comparator_13 (
    .a(harf_sayisi), .b(4'b0100), .eq(comparator_13_eq));  // open: gt, lt
  Comparator #(.width(4), .mode("unsigned")) comparator_14 (
    .a(harf_sayisi), .b(4'b0101), .eq(comparator_14_eq));  // open: gt, lt
  Comparator #(.width(4), .mode("unsigned")) comparator_15 (
    .a(harf_sayisi), .b(4'b0110), .eq(comparator_15_eq));  // open: gt, lt
  Comparator #(.width(4), .mode("unsigned")) comparator_16 (
    .a(harf_sayisi), .b(4'b0111), .eq(comparator_16_eq));  // open: gt, lt
  Comparator #(.width(4), .mode("unsigned")) comparator_17 (
    .a(harf_sayisi), .b(4'b1000), .eq(comparator_17_eq));  // open: gt, lt
  or u_c (c, comparator_9_eq, comparator_10_eq, comparator_11_eq, comparator_12_eq, comparator_13_eq, comparator_16_eq, comparator_17_eq);
  or u_a (a, comparator_9_eq, comparator_11_eq, comparator_12_eq, comparator_17_eq, comparator_14_eq, comparator_15_eq, comparator_16_eq);
  or u_b (b, comparator_9_eq, comparator_13_eq, comparator_14_eq, comparator_15_eq, comparator_17_eq);
  or u_d (d, comparator_11_eq, comparator_12_eq, comparator_13_eq, comparator_14_eq, comparator_15_eq, comparator_17_eq);
  or u_e (e, comparator_9_eq, comparator_11_eq, comparator_15_eq, comparator_17_eq);
  or u_g (g, comparator_9_eq, comparator_11_eq, comparator_12_eq, comparator_14_eq, comparator_15_eq, comparator_17_eq);
  or u_f (f, comparator_9_eq, comparator_10_eq, comparator_12_eq, comparator_13_eq, comparator_14_eq, comparator_15_eq, comparator_16_eq, comparator_17_eq);
endmodule
