// Logisim project adam.circ as structural Verilog: 1 circuit, main circuit main
module main (
  input  [4:0] in_1,
  output [7:0] _1,
  output [7:0] _2,
  output [7:0] _3,
  output [7:0] _4,
  output [7:0] _5
);

  wire [3:0] bit_extender_1_out;

  Bit_Extender #(.in_width(5), .out_width(4)) bit_extender_1 (.in(in_1), .out(bit_extender_1_out));
  Multiplexer #(.select(4), .width(8), .enable("false")) multiplexer_1 (
    .in0({8{1'b0}}), .in1(8'h1), .in2({8{1'b1}}), .in3({8{1'b1}}), .in4({8{1'b1}}), .in5({8{1'b1}}),
    .in6({8{1'b1}}), .in7({8{1'b1}}), .in8({8{1'b1}}), .in9({8{1'b1}}), .in10({8{1'b1}}), .in11({8{1'b1}}),
    .in12({8{1'b1}}), .in13({8{1'b1}}), .in14({8{1'b1}}), .in15({8{1'b1}}), .out(_1), .sel(bit_extender_1_out));
  Multiplexer #(.select(4), .width(8), .enable("false")) multiplexer_2 (
    .in0({8{1'b0}}), .in1(8'h1), .in2(8'h1), .in3(8'h81), .in4(8'h81), .in5(8'h81), .in6(8'h81), .in7(8'h81),
    .in8(8'h81), .in9(8'h81), .in10(8'h81), .in11(8'h81), .in12(8'h81), .in13(8'h81), .in14(8'h81),
    .in15(8'h81), .out(_2), .sel(bit_extender_1_out));
  Multiplexer #(.select(4), .width(8), .enable("false")) multiplexer_3 (
    .in0({8{1'b0}}), .in1(8'h1), .in2(8'h1), .in3(8'h81), .in4(8'h81), .in5(8'ha1), .in6(8'ha1), .in7(8'ha1),
    .in8(8'ha1), .in9(8'ha9), .in10(8'ha9), .out(_3), .sel(bit_extender_1_out));  // open: in11, in12, in13, in14, in15
  Multiplexer #(.select(4), .width(8), .enable("false")) multiplexer_4 (
    .in0({8{1'b0}}), .in1({8{1'b0}}), .in2({8{1'b0}}), .in3(8'h80), .in4(8'hc0), .in5(8'hc0), .in6(8'hc0),
    .in7(8'he0), .in8(8'hf0), .in9(8'hf0), .in10(8'hf0), .in11(8'hf0), .in12(8'hf0), .in13(8'hf0),
    .in14(8'hf0), .in15(8'hf0), .out(_4), .sel(bit_extender_1_out));
  Multiplexer #(.select(4), .width(8), .enable("false")) multiplexer_5 (
    .in0({8{1'b0}}), .in1({8{1'b0}}), .in2({8{1'b0}}), .in3({8{1'b0}}), .in4({8{1'b0}}), .in5({8{1'b0}}),
    .in6(8'h20), .in7(8'h20), .in8(8'h20), .in9(8'h20), .in10(8'h28), .in11(8'h28), .in12(8'h28),
    .in13(8'h28), .in14(8'h28), .in15(8'h28), .out(_5), .sel(bit_extender_1_out));
endmodule
