// Logisim project buttons.circ as structural Verilog: 1 circuit, main circuit main
module main (
  input  \input ,
  input  clock,
  output \output 
);

  wire and_2_out, and_3_out, not_1_out, not_2_out, not_3_out, not_4_out, not_5_out;
  wire [1:0] and_4_out, register_1_q;

  not not_1 (not_1_out, register_1_q[1]);
  not not_2 (not_2_out, register_1_q[1]);
  not not_3 (not_3_out, register_1_q[0]);
  not not_4 (not_4_out, register_1_q[1]);
  not not_5 (not_5_out, register_1_q[0]);
  and and_1 (\output , not_1_out, register_1_q[0]);
  and and_2 (and_2_out, \input , not_2_out, register_1_q[0]);
  and and_3 (and_3_out, \input , not_3_out, register_1_q[1]);
  and and_4 (and_4_out[0], \input , not_4_out, not_5_out);
  Register #(.width(2)) register_1 (.D(and_4_out), .en(1'b1), .Q(register_1_q), .clk(clock));  // open: clr
  or or_1 (and_4_out[1], and_2_out, and_3_out);
endmodule
