// Logisim project controller.circ as structural Verilog: 1 circuit, main circuit main
module main (
  input  Reset,
  input  IV,
  input  HV,
  input  VAR,
  input  YOK,
  input  OVAR,
  input  OYOK,
  input  Y10,
  input  GT,
  input  BIT,
  input  clock,
  output [3:0] out_12,
  output Lin,
  output DC,
  output BU,
  output SAYR,
  output LC,
  output LY,
  output SCC,
  output RTTY,
  output CVPY,
  output AR,
  output ETTY,
  output DCVP,
  output Sch
);

  wire and_5_out, and_9_out, and_10_out, and_11_out, and_12_out, and_13_out, and_14_out, and_15_out,
       and_16_out, and_17_out, and_18_out, and_19_out, and_20_out, and_21_out, and_22_out, and_23_out,
       and_24_out, and_25_out, not_1_out, not_2_out, not_3_out, not_4_out, not_5_out, not_6_out, not_7_out,
       not_8_out, not_9_out, not_10_out, not_11_out, not_12_out, not_13_out, not_14_out, not_15_out,
       not_16_out, not_17_out, not_18_out, not_19_out, not_20_out, not_21_out, not_22_out, not_23_out,
       not_24_out, not_25_out, not_26_out, not_27_out, not_28_out, not_29_out, not_30_out, not_31_out,
       not_32_out, not_33_out, not_34_out, not_35_out, not_36_out, not_37_out, not_38_out, not_39_out,
       not_40_out, not_41_out, not_42_out, not_43_out, not_44_out, not_45_out, not_46_out, not_47_out,
       not_48_out, not_49_out, not_50_out, not_51_out, not_52_out, not_53_out, not_54_out, not_55_out,
       not_56_out, not_57_out, not_58_out, not_59_out, not_60_out, not_61_out, not_62_out, not_63_out,
       not_64_out, not_65_out, not_66_out, not_67_out, not_68_out, not_69_out, not_70_out, not_71_out,
       or_7_out;
  wire [3:0] or_6_out;

  Register #(.width(4)) register_1 (.D(or_6_out), .Q(out_12), .clk(clock));  // open: en, clr
  not not_1 (not_1_out, out_12[3]);
  not not_2 (not_2_out, out_12[2]);
  not not_3 (not_3_out, out_12[1]);
  not not_4 (not_4_out, out_12[0]);
  not not_5 (not_5_out, out_12[3]);
  not not_6 (not_6_out, out_12[2]);
  not not_7 (not_7_out, out_12[0]);
  not not_8 (not_8_out, out_12[3]);
  not not_9 (not_9_out, out_12[2]);
  not not_10 (not_10_out, out_12[3]);
  not not_11 (not_11_out, out_12[1]);
  not not_12 (not_12_out, out_12[2]);
  not not_13 (not_13_out, out_12[1]);
  not not_14 (not_14_out, out_12[0]);
  not not_15 (not_15_out, out_12[3]);
  not not_16 (not_16_out, out_12[0]);
  not not_17 (not_17_out, out_12[2]);
  not not_18 (not_18_out, out_12[1]);
  not not_19 (not_19_out, out_12[2]);
  not not_20 (not_20_out, out_12[1]);
  not not_21 (not_21_out, out_12[0]);
  not not_22 (not_22_out, out_12[2]);
  not not_23 (not_23_out, out_12[1]);
  not not_24 (not_24_out, Reset);
  not not_25 (not_25_out, out_12[3]);
  not not_26 (not_26_out, out_12[1]);
  not not_27 (not_27_out, out_12[3]);
  not not_28 (not_28_out, out_12[2]);
  not not_29 (not_29_out, out_12[1]);
  not not_30 (not_30_out, out_12[0]);
  not not_31 (not_31_out, out_12[3]);
  not not_32 (not_32_out, out_12[2]);
  not not_33 (not_33_out, out_12[0]);
  not not_34 (not_34_out, out_12[3]);
  not not_35 (not_35_out, out_12[2]);
  not not_36 (not_36_out, out_12[3]);
  not not_37 (not_37_out, out_12[1]);
  not not_38 (not_38_out, out_12[0]);
  not not_39 (not_39_out, out_12[3]);
  not not_40 (not_40_out, out_12[0]);
  not not_41 (not_41_out, out_12[3]);
  not not_42 (not_42_out, out_12[2]);
  not not_43 (not_43_out, out_12[1]);
  not not_44 (not_44_out, YOK);
  not not_45 (not_45_out, OVAR);
  not not_46 (not_46_out, out_12[3]);
  not not_47 (not_47_out, out_12[2]);
  not not_48 (not_48_out, out_12[1]);
  not not_49 (not_49_out, VAR);
  not not_50 (not_50_out, out_12[3]);
  not not_51 (not_51_out, out_12[1]);
  not not_52 (not_52_out, out_12[0]);
  not not_53 (not_53_out, out_12[3]);
  not not_54 (not_54_out, out_12[2]);
  not not_55 (not_55_out, out_12[1]);
  not not_56 (not_56_out, out_12[0]);
  not not_57 (not_57_out, out_12[3]);
  not not_58 (not_58_out, out_12[2]);
  not not_59 (not_59_out, out_12[1]);
  not not_60 (not_60_out, VAR);
  not not_61 (not_61_out, out_12[3]);
  not not_62 (not_62_out, out_12[2]);
  not not_63 (not_63_out, out_12[3]);
  not not_64 (not_64_out, out_12[1]);
  not not_65 (not_65_out, out_12[0]);
  not not_66 (not_66_out, GT);
  not not_67 (not_67_out, out_12[3]);
  not not_68 (not_68_out, out_12[1]);
  not not_69 (not_69_out, out_12[2]);
  not not_70 (not_70_out, out_12[1]);
  not not_71 (not_71_out, out_12[0]);
  and and_1 (Lin, not_1_out, not_2_out, not_3_out, not_4_out);
  and and_2 (BU, not_5_out, not_6_out, out_12[1], not_7_out);
  and and_3 (LC, not_8_out, not_9_out, out_12[1], out_12[0]);
  and and_4 (SCC, not_10_out, out_12[2], not_11_out, out_12[0]);
  and and_5 (and_5_out, out_12[3], not_12_out, not_13_out, not_14_out);
  and and_6 (AR, not_15_out, out_12[2], out_12[1], not_16_out);
  and and_7 (DCVP, out_12[3], not_17_out, not_18_out, out_12[0]);
  and and_8 (Sch, out_12[3], not_19_out, not_20_out, not_21_out);
  and and_9 (and_9_out, out_12[3], not_22_out, not_23_out, out_12[0], not_24_out);
  and and_10 (and_10_out, not_25_out, out_12[2], not_26_out, out_12[0]);
  and and_11 (and_11_out, not_27_out, out_12[2], out_12[1], out_12[0], BIT);
  and and_12 (and_12_out, out_12[3], not_28_out, not_29_out, not_30_out);
  and and_13 (and_13_out, not_31_out, not_32_out, out_12[1], not_33_out);
  and and_14 (and_14_out, not_34_out, not_35_out, out_12[1], out_12[0], Y10);
  and and_15 (and_15_out, not_36_out, out_12[2], not_37_out, not_38_out);
  and and_16 (and_16_out, not_39_out, out_12[1], out_12[1], not_40_out);
  and and_17 (and_17_out, not_41_out, not_42_out, not_43_out, out_12[0], VAR, not_44_out, not_45_out, OYOK);
  and and_18 (and_18_out, not_46_out, not_47_out, not_48_out, out_12[0], not_49_out, YOK);
  and and_19 (and_19_out, not_50_out, out_12[2], not_51_out, not_52_out);
  and and_20 (and_20_out, not_53_out, not_54_out, not_55_out, not_56_out, IV, HV);
  and and_21 (and_21_out, not_57_out, not_58_out, not_59_out, out_12[0], not_60_out, YOK);
  and and_22 (and_22_out, not_61_out, not_62_out, out_12[1], out_12[0], Y10);
  and and_23 (and_23_out, not_63_out, out_12[2], not_64_out, not_65_out, not_66_out);
  and and_24 (and_24_out, not_67_out, out_12[2], not_68_out, out_12[0]);
  and and_25 (and_25_out, out_12[3], not_69_out, not_70_out, not_71_out);
  or or_1 (CVPY, SCC, and_5_out);
  or or_2 (ETTY, AR, DCVP);
  or or_3 (or_6_out[3], and_9_out, and_10_out, and_11_out, and_12_out);
  or or_4 (or_6_out[2], and_13_out, and_14_out, and_15_out, and_16_out);
  or or_5 (or_6_out[1], and_17_out, and_18_out, and_19_out);
  or or_6 (or_6_out[0], and_20_out, and_21_out, and_22_out, and_9_out, and_23_out, and_24_out, and_25_out);
  or or_7 (or_7_out, CVPY, Reset);
  D_Flip_Flop d_ff_1 (.clk(clock), .D(or_7_out), .Q(RTTY));  // open: Qn, preset, en, reset

  assign DC = BU;
  assign LY = LC;
  assign SAYR = BU;
endmodule
