// Logisim project gameDatapath.circ as structural Verilog: 1 circuit, main circuit main
module main (
  input  CVPY,
  input  ScH,
  input  [3:0] harf_sayisi,
  input  DCVP,
  input  a,
  input  SAYR,
  input  AR,
  input  b,
  input  BU,
  input  c,
  input  DC,
  input  reset,
  input  d,
  input  e,
  input  f,
  input  g,
  input  h,
  input  ScoreReset,
  input  i,
  input  j,
  input  [7:0] R1,
  input  k,
  input  [7:0] R2,
  input  l,
  input  [7:0] R3,
  input  m,
  input  n,
  input  o,
  input  p,
  input  [7:0] R4,
  input  q,
  input  r,
  input  [7:0] R5,
  input  s,
  input  t,
  input  [7:0] R6,
  input  u,
  input  Lin,
  input  v,
  input  [7:0] R7,
  input  w,
  input  x,
  input  y,
  input  [7:0] R8,
  input  z,
  input  LY,
  input  clock,
  input  LC,
  input  ScC,
  output harfVarmi,
  output [3:0] HumanScore,
  output [6:0] TTYGIRISI,
  output Bit,
  output GT,
  output inputVarmi,
  output VAR,
  output YOK,
  output OVAR,
  output OYOK,
  output L1,
  output L2,
  output L3,
  output L4,
  output L5,
  output L6,
  output L7,
  output L8,
  output L9,
  output L10,
  output [4:0] yanlisSayisi,
  output Y10,
  output [3:0] ComputerScor
);

  wire comparator_1_gt, d_ff_1_q;
  wire [3:0] adder_1_out, counter_1_q, counter_4_q, main_2_toplami, main_3_toplami, register_2_q;
  wire [4:0] priority_encoder_1_out;
  wire [6:0] bit_extender_1_out, bit_extender_2_out;
  wire [7:0] multiplexer_1_out, register_1_q, shift_register_1_q0, shift_register_1_q1, shift_register_1_q2,
       shift_register_1_q3, shift_register_1_q4, shift_register_1_q5, shift_register_1_q6,
       shift_register_1_q7;

  Priority_Encoder #(.select(5)) priority_encoder_1 (
    .in0(1'b1), .in1(a), .in2(b), .in3(c), .in4(d), .in5(e), .in6(f), .in7(g), .in8(h), .in9(i), .in10(j),
    .in11(k), .in12(l), .in13(m), .in14(n), .in15(o), .in16(p), .in17(q), .in18(r), .in19(s), .in20(t),
    .in21(u), .in22(v), .in23(w), .in24(x), .in25(y), .in26(z), .out(priority_encoder_1_out));  // open: in27, in28, in29, in30, in31, gs, en_out, en_in
  Comparator #(.width(5), .mode("unsigned")) comparator_1 (
    .a(priority_encoder_1_out), .b({5{1'b0}}), .gt(comparator_1_gt));  // open: eq, lt
  buttons_main main_1 (.\input (comparator_1_gt), .clock(clock), .\output (inputVarmi));
  Multiplexer #(.select(4), .width(8), .enable("false")) multiplexer_1 (
    .in0({8{1'b0}}), .in1(R1), .in2(R2), .in3(R3), .in4(R4), .in5(R5), .in6(R6), .in7(R7), .in8(R8),
    .in9({8{1'b0}}), .in10({8{1'b0}}), .in11({8{1'b0}}), .in12({8{1'b0}}), .in13({8{1'b0}}),
    .in14({8{1'b0}}), .in15({8{1'b0}}), .out(multiplexer_1_out), .sel(counter_1_q));
  Counter #(.width(4), .max('h9), .ongoal("stay")) counter_1 (
    .Q(counter_1_q), .clk(clock), .clr(CVPY));  // open: load, D, count, carry
  Register register_1 (.D({3'b011, priority_encoder_1_out}), .en(Lin), .Q(register_1_q), .clk(clock));  // open: clr
  Comparator #(.width(4), .mode("unsigned")) comparator_2 (
    .a(harf_sayisi), .b(4'b0000), .gt(harfVarmi));  // open: eq, lt
  harfsayacim_main main_2 (
    .\input (register_1_q), .in_2(R1), .in_3(R2), .in_4(R3), .in_5(R4), .in_6(R5), .in_7(R6), .in_8(R7),
    .in_9(R8), .toplami(main_2_toplami));
  harfsayacim_main main_3 (
    .\input (register_1_q), .in_2(shift_register_1_q1), .in_3(shift_register_1_q2),
    .in_4(shift_register_1_q3), .in_5(shift_register_1_q4), .in_6(shift_register_1_q5),
    .in_7(shift_register_1_q6), .in_8(shift_register_1_q7), .in_9(shift_register_1_q0),
    .toplami(main_3_toplami));
  Comparator #(.width(4), .mode("unsigned")) comparator_3 (
    .a(harf_sayisi), .b(register_2_q), .eq(Bit));  // open: gt, lt
  Comparator #(.width(4), .mode("unsigned")) comparator_4 (
    .a(main_2_toplami), .b(4'b0000), .gt(VAR), .eq(YOK));  // open: lt
  Comparator #(.width(4), .mode("unsigned")) comparator_5 (
    .a(main_3_toplami), .b(4'b0000), .gt(OVAR), .eq(OYOK));  // open: lt
  Register #(.width(4)) register_2 (.D(adder_1_out), .Q(register_2_q), .clk(DC), .clr(reset));  // open: en
  Adder #(.width(4)) adder_1 (.a(register_2_q), .b(main_2_toplami), .out(adder_1_out));  // open: cin, cout
  Bit_Extender #(.out_width(7)) bit_extender_1 (.in(register_1_q), .out(bit_extender_1_out));
  Counter #(.width(4), .max('hf)) counter_2 (
    .Q(HumanScore), .clk(ScH), .clr(ScoreReset));  // open: load, D, count, carry
  Counter #(.width(5), .max('h1f)) counter_3 (.Q(yanlisSayisi), .clk(LC), .clr(reset));  // open: load, D, count, carry
  Shift_Register #(.width(8)) shift_register_1 (
    .shift(BU), .in(register_1_q), .clk(clock), .clr(reset), .q0(shift_register_1_q0),
    .q1(shift_register_1_q1), .q2(shift_register_1_q2), .q3(shift_register_1_q3), .q4(shift_register_1_q4),
    .q5(shift_register_1_q5), .q6(shift_register_1_q6), .q7(shift_register_1_q7));  // open: out, load, d0, d1, d2, d3, d4, d5, d6, d7
  Comparator #(.width(5), .mode("unsigned")) comparator_6 (.a(yanlisSayisi), .b(5'b01010), .eq(Y10));  // open: gt, lt
  Counter #(.width(4), .max('hf), .ongoal("stay"), .trigger("falling")) counter_4 (
    .Q(counter_4_q), .clk(AR), .clr(SAYR));  // open: load, D, count, carry
  Comparator #(.width(4), .mode("unsigned")) comparator_7 (
    .a(main_2_toplami), .b(counter_4_q), .gt(GT));  // open: eq, lt
  Shift_Register #(.length(10)) shift_register_2 (
    .in(1'b1), .clk(LY), .clr(reset), .q0(L1), .q1(L2), .q2(L3), .q3(L4), .q4(L5), .q5(L6), .q6(L7), .q7(L8),
    .q8(L9), .q9(L10));  // open: shift, out, load, d0, d1, d2, d3, d4, d5, d6, d7, d8, d9
  D_Flip_Flop d_ff_1 (.clk(clock), .D(ScC), .Q(d_ff_1_q));  // open: Qn, preset, en, reset
  Counter #(.width(4), .max('hf)) counter_5 (
    .Q(ComputerScor), .clk(d_ff_1_q), .clr(ScoreReset));  // open: load, D, count, carry
  Bit_Extender #(.out_width(7)) bit_extender_2 (.in(multiplexer_1_out), .out(bit_extender_2_out));
  Multiplexer #(.width(7), .enable("false")) multiplexer_2 (
    .in0(bit_extender_1_out), .in1(bit_extender_2_out), .out(TTYGIRISI), .sel(DCVP));

  // Notes on the sheet:
  //   Tamamini dogru bilince 1 oluyor
endmodule
