// Logisim project hangman.circ as structural Verilog: 1 circuit, main circuit main
module main (
  output [3:0] out_1,
  output [7:0] R1,
  output [7:0] R2,
  output [7:0] R3,
  output [7:0] R4,
  output [7:0] R5,
  output [7:0] R6,
  output [7:0] R7,
  output [7:0] R8
);

  wire a_2_out, a_out, b_2_out, b_out, c_2_out, c_out, clock_1_out, d_2_out, d_out, e_2_out, e_out, f_2_out,
       f_out, g_2_out, g_out, h_2_out, h_out, i_2_out, i_out, j_2_out, j_out, k_2_out, k_out, l_2_out, l_out,
       m_2_out, m_out, main_1_a_2, main_1_b_2, main_1_c_2, main_1_d_2, main_1_e_2, main_1_f_2, main_1_g_2,
       main_2_a, main_2_b, main_2_c, main_2_d, main_2_e, main_2_f, main_2_g, main_3_bit, main_3_gt,
       main_3_harfvarmi, main_3_inputvarmi, main_3_l1, main_3_l2, main_3_l3, main_3_l4, main_3_l5, main_3_l6,
       main_3_l7, main_3_l8, main_3_l9, main_3_l10, main_3_ovar, main_3_oyok, main_3_var, main_3_y10,
       main_3_yok, main_5_a, main_5_b, main_5_c, main_5_d, main_5_e, main_5_f, main_5_g, main_6_ar,
       main_6_bu, main_6_cvpy, main_6_dc, main_6_dcvp, main_6_etty, main_6_lc, main_6_lin, main_6_ly,
       main_6_rtty, main_6_sayr, main_6_scc, main_6_sch, n_2_out, n_out, o_2_out, o_out, p_2_out, p_out,
       q_2_out, q_out, r_2_out, r_out, Reset_Game_out, s_2_out, s_out, ScoreReset_out, t_2_out, t_out,
       u_2_out, u_out, v_2_out, v_out, w_2_out, w_out, x_2_out, x_out, y_2_out, y_out, z_2_out, z_out;
  wire [3:0] main_1_harf_sayisi, main_3_computerscor, main_3_humanscore;
  wire [4:0] main_3_yanlissayisi;
  wire [6:0] main_3_ttygirisi;
  wire [7:0] main_4__1, main_4__2, main_4__3, main_4__4, main_4__5;

  Button a (.out(a_out));
  Button b (.out(b_out));
  Button c (.out(c_out));
  Button d (.out(d_out));
  Button e (.out(e_out));
  Button f (.out(f_out));
  Button g (.out(g_out));
  Button h (.out(h_out));
  Button i (.out(i_out));
  Button j (.out(j_out));
  Button k (.out(k_out));
  Button l (.out(l_out));
  Button m (.out(m_out));
  Button n (.out(n_out));
  Button o (.out(o_out));
  Button p (.out(p_out));
  Button q (.out(q_out));
  Button r (.out(r_out));
  Button s (.out(s_out));
  Button t (.out(t_out));
  Button u (.out(u_out));
  Button v (.out(v_out));
  Button w (.out(w_out));
  Button x (.out(x_out));
  Button y (.out(y_out));
  Button z (.out(z_out));
  input_main main_1 (
    .a(a_out), .b(b_out), .c(c_out), .d(d_out), .e(e_out), .f(f_out), .g(g_out), .h(h_out), .i(i_out),
    .j(j_out), .k(k_out), .l(l_out), .m(m_out), .n(n_out), .o(o_out), .p(p_out), .q(q_out), .r(r_out),
    .s(s_out), .t(t_out), .u(u_out), .v(v_out), .w(w_out), .x(x_out), .y(y_out), .z(z_out),
    .clock(clock_1_out), .reset(Reset_Game_out), .harf_sayisi(main_1_harf_sayisi), .c_2(main_1_c_2), .R1(R1),
    .a_2(main_1_a_2), .R2(R2), .b_2(main_1_b_2), .R3(R3), .d_2(main_1_d_2), .R4(R4), .e_2(main_1_e_2),
    .R5(R5), .g_2(main_1_g_2), .R6(R6), .f_2(main_1_f_2), .R7(R7), .R8(R8));
  _7_Segment_Display u_7_segment_display_1 (
    .g(main_1_d_2), .f(main_1_b_2), .a(main_1_a_2), .b(main_1_c_2), .e(main_1_e_2), .d(main_1_g_2),
    .c(main_1_f_2));  // open: dp
  Button a_2 (.out(a_2_out));
  Button b_2 (.out(b_2_out));
  Button c_2 (.out(c_2_out));
  Button d_2 (.out(d_2_out));
  Button e_2 (.out(e_2_out));
  Button f_2 (.out(f_2_out));
  Button g_2 (.out(g_2_out));
  Button h_2 (.out(h_2_out));
  Button i_2 (.out(i_2_out));
  Button j_2 (.out(j_2_out));
  Button k_2 (.out(k_2_out));
  Button l_2 (.out(l_2_out));
  Button m_2 (.out(m_2_out));
  Button n_2 (.out(n_2_out));
  Button o_2 (.out(o_2_out));
  Button p_2 (.out(p_2_out));
  Button q_2 (.out(q_2_out));
  Button r_2 (.out(r_2_out));
  Button s_2 (.out(s_2_out));
  Button t_2 (.out(t_2_out));
  Button u_2 (.out(u_2_out));
  Button v_2 (.out(v_2_out));
  Button w_2 (.out(w_2_out));
  Button x_2 (.out(x_2_out));
  Button y_2 (.out(y_2_out));
  Button z_2 (.out(z_2_out));
  LED led_1 (.in(main_3_l1));
  LED led_2 (.in(main_3_l3));
  LED led_3 (.in(main_3_l4));
  LED led_4 (.in(main_3_l2));
  scor_main main_2 (
    .sayi(main_3_humanscore), .c(main_2_c), .a(main_2_a), .b(main_2_b), .d(main_2_d), .e(main_2_e),
    .g(main_2_g), .f(main_2_f));
  LED led_5 (.in(main_3_l5));
  LED led_6 (.in(main_3_l6));
  LED led_7 (.in(main_3_l8));
  LED led_8 (.in(main_3_l7));
  _7_Segment_Display u_7_segment_display_2 (
    .g(main_2_d), .f(main_2_b), .a(main_2_a), .b(main_2_c), .e(main_2_e), .d(main_2_g), .c(main_2_f));  // open: dp
  gameDatapath_main main_3 (
    .ScH(main_6_sch), .harf_sayisi(main_1_harf_sayisi), .a(a_2_out), .AR(main_6_ar), .b(b_2_out),
    .c(c_2_out), .DC(main_6_dc), .d(d_2_out), .e(e_2_out), .f(f_2_out), .g(g_2_out), .h(h_2_out),
    .i(i_2_out), .j(j_2_out), .R1(R1), .k(k_2_out), .R2(R2), .l(l_2_out), .R3(R3), .m(m_2_out), .n(n_2_out),
    .o(o_2_out), .p(p_2_out), .R4(R4), .q(q_2_out), .r(r_2_out), .R5(R5), .s(s_2_out), .t(t_2_out), .R6(R6),
    .u(u_2_out), .Lin(main_6_lin), .v(v_2_out), .R7(R7), .w(w_2_out), .x(x_2_out), .y(y_2_out), .R8(R8),
    .z(z_2_out), .LY(main_6_ly), .clock(clock_1_out), .LC(main_6_lc), .ScC(main_6_scc),
    .inputVarmi(main_3_inputvarmi), .L1(main_3_l1), .L2(main_3_l2), .L3(main_3_l3), .L4(main_3_l4),
    .L5(main_3_l5), .L6(main_3_l6), .L7(main_3_l7), .L8(main_3_l8), .L9(main_3_l9), .L10(main_3_l10),
    .harfVarmi(main_3_harfvarmi), .HumanScore(main_3_humanscore), .CVPY(main_6_cvpy),
    .TTYGIRISI(main_3_ttygirisi), .Bit(main_3_bit), .DCVP(main_6_dcvp), .GT(main_3_gt), .SAYR(main_6_sayr),
    .BU(main_6_bu), .reset(Reset_Game_out), .ScoreReset(ScoreReset_out), .VAR(main_3_var), .YOK(main_3_yok),
    .OVAR(main_3_ovar), .OYOK(main_3_oyok), .yanlisSayisi(main_3_yanlissayisi), .Y10(main_3_y10),
    .ComputerScor(main_3_computerscor));
  LED led_9 (.in(main_3_l10));
  LED led_10 (.in(main_3_l9));
  Button ScoreReset (.out(ScoreReset_out));
  Button Reset_Game (.out(Reset_Game_out));
  adam_main main_4 (
    .in_1(main_3_yanlissayisi), ._1(main_4__1), ._4(main_4__4), ._2(main_4__2), ._3(main_4__3), ._5(main_4__5));
  scor_main main_5 (
    .sayi(main_3_computerscor), .c(main_5_c), .a(main_5_a), .b(main_5_b), .d(main_5_d), .e(main_5_e),
    .g(main_5_g), .f(main_5_f));
  _7_Segment_Display u_7_segment_display_3 (
    .g(main_5_d), .f(main_5_b), .a(main_5_a), .b(main_5_c), .e(main_5_e), .d(main_5_g), .c(main_5_f));  // open: dp
  controller_main main_6 (
    .IV(main_3_inputvarmi), .HV(main_3_harfvarmi), .VAR(main_3_var), .YOK(main_3_yok), .OVAR(main_3_ovar),
    .OYOK(main_3_oyok), .Y10(main_3_y10), .GT(main_3_gt), .BIT(main_3_bit), .clock(clock_1_out),
    .Reset(Reset_Game_out), .out_12(out_1), .Lin(main_6_lin), .DC(main_6_dc), .BU(main_6_bu),
    .SAYR(main_6_sayr), .LC(main_6_lc), .LY(main_6_ly), .SCC(main_6_scc), .RTTY(main_6_rtty),
    .CVPY(main_6_cvpy), .AR(main_6_ar), .ETTY(main_6_etty), .DCVP(main_6_dcvp), .Sch(main_6_sch));
  DotMatrix #(.matrixrows(8)) dotmatrix_1 (
    .col0(main_4__1), .col1(main_4__2), .col2(main_4__3), .col3(main_4__4), .col4(main_4__5));
  Clock clock_1 (.out(clock_1_out));
  TTY tty_1 (.data(main_3_ttygirisi), .clk(clock_1_out), .we(main_6_etty), .clr(main_6_rtty));

  // Notes on the sheet:
  //   LETTERS COUNT
  //   Human Score
  //   ComputerScore
endmodule
