// Logisim project input.circ as structural Verilog: 1 circuit, main circuit main
module main (
  input  reset,
  input  a,
  input  b,
  input  c,
  input  d,
  input  e,
  input  f,
  input  g,
  input  h,
  input  i,
  input  j,
  input  k,
  input  l,
  input  m,
  input  n,
  input  o,
  input  p,
  input  q,
  input  r,
  input  s,
  input  t,
  input  u,
  input  v,
  input  w,
  input  x,
  input  y,
  input  z,
  input  clock,
  output [3:0] harf_sayisi,
  output c_2,
  output [7:0] R1,
  output a_2,
  output [7:0] R2,
  output b_2,
  output [7:0] R3,
  output d_2,
  output [7:0] R4,
  output e_2,
  output [7:0] R5,
  output g_2,
  output [7:0] R6,
  output f_2,
  output [7:0] R7,
  output [7:0] R8
);

  wire comparator_1_gt, main_1_output;
  wire [4:0] priority_encoder_1_out;
  wire [7:0] register_1_q;

  Priority_Encoder #(.select(5)) priority_encoder_1 (
    .in0(1'b1), .in1(a), .in2(b), .in3(c), .in4(d), .in5(e), .in6(f), .in7(g), .in8(h), .in9(i), .in10(j),
    .in11(k), .in12(l), .in13(m), .in14(n), .in15(o), .in16(p), .in17(q), .in18(r), .in19(s), .in20(t),
    .in21(u), .in22(v), .in23(w), .in24(x), .in25(y), .in26(z), .out(priority_encoder_1_out));  // open: in27, in28, in29, in30, in31, gs, en_out, en_in
  Comparator #(.width(5), .mode("unsigned")) comparator_1 (
    .a(priority_encoder_1_out), .b({5{1'b0}}), .gt(comparator_1_gt));  // open: eq, lt
  buttons_main main_1 (.\input (comparator_1_gt), .clock(clock), .\output (main_1_output));
  Register register_1 (
    .D({3'b011, priority_encoder_1_out}), .en(comparator_1_gt), .Q(register_1_q), .clk(clock));  // open: clr
  Shift_Register #(.width(8)) shift_register_1 (
    .shift(main_1_output), .in(register_1_q), .clk(clock), .clr(reset), .q0(R8), .q1(R7), .q2(R6), .q3(R5),
    .q4(R4), .q5(R3), .q6(R2), .q7(R1));  // open: out, load, d0, d1, d2, d3, d4, d5, d6, d7
  _7segment_main main_2 (
    .in_1(R1), .in_2(R2), .in_3(R3), .in_4(R4), .in_5(R5), .in_6(R6), .in_7(R7), .in_8(R8), .c(c_2), .a(a_2),
    .harf_sayisi(harf_sayisi), .b(b_2), .d(d_2), .e(e_2), .g(g_2), .f(f_2));
endmodule
