// Logisim project scor.circ as structural Verilog: 1 circuit, main circuit main
module main (
  input  [3:0] sayi,
  output c,
  output a,
  output b,
  output d,
  output e,
  output g,
  output f
);

  wire comparator_1_eq, comparator_2_eq, comparator_3_eq, comparator_4_eq, comparator_5_eq, comparator_6_eq,
       comparator_7_eq, comparator_8_eq, comparator_9_eq;

  Comparator #(.width(4), .mode("unsigned")) comparator_1 (
    .a(sayi), .b(4'b0000), .eq(comparator_1_eq));  // open: gt, lt
  Comparator #(.width(4), .mode("unsigned")) comparator_2 (
    .a(sayi), .b(4'b0001), .eq(comparator_2_eq));  // open: gt, lt
  Comparator #(.width(4), .mode("unsigned")) comparator_3 (
    .a(sayi), .b(4'b0010), .eq(comparator_3_eq));  // open: gt, lt
  Comparator #(.width(4), .mode("unsigned")) comparator_4 (
    .a(sayi), .b(4'b0011), .eq(comparator_4_eq));  // open: gt, lt
  Comparator #(.width(4), .mode("unsigned")) comparator_5 (
    .a(sayi), .b(4'b0100), .eq(comparator_5_eq));  // open: gt, lt
  Comparator #(.width(4), .mode("unsigned")) comparator_6 (
    .a(sayi), .b(4'b0101), .eq(comparator_6_eq));  // open: gt, lt
  Comparator #(.width(4), .mode("unsigned")) comparator_7 (
    .a(sayi), .b(4'b0110), .eq(comparator_7_eq));  // open: gt, lt
  Comparator #(.width(4), .mode("unsigned")) comparator_8 (
    .a(sayi), .b(4'b0111), .eq(comparator_8_eq));  // open: gt, lt
  Comparator #(.width(4), .mode("unsigned")) comparator_9 (
    .a(sayi), .b(4'b1000), .eq(comparator_9_eq));  // open: gt, lt
  or u_c (c, comparator_1_eq, comparator_2_eq, comparator_3_eq, comparator_4_eq, comparator_5_eq, comparator_8_eq, comparator_9_eq);
  or u_a (a, comparator_1_eq, comparator_3_eq, comparator_4_eq, comparator_9_eq, comparator_6_eq, comparator_7_eq, comparator_8_eq);
  or u_b (b, comparator_1_eq, comparator_5_eq, comparator_6_eq, comparator_7_eq, comparator_9_eq);
  or u_d (d, comparator_3_eq, comparator_4_eq, comparator_5_eq, comparator_6_eq, comparator_7_eq, comparator_9_eq);
  or u_e (e, comparator_1_eq, comparator_3_eq, comparator_7_eq, comparator_9_eq);
  or u_g (g, comparator_1_eq, comparator_3_eq, comparator_4_eq, comparator_6_eq, comparator_7_eq, comparator_9_eq);
  or u_f (f, comparator_1_eq, comparator_2_eq, comparator_4_eq, comparator_5_eq, comparator_6_eq, comparator_7_eq, comparator_8_eq, comparator_9_eq);
endmodule
